// Logisim project ex2.circ as structural Verilog: 6 circuits, main circuit AND2
module AND2 (
  input  A,
  input  B,
  output RESULT
);

  and and_1 (RESULT, A, B);

  // Notes on the sheet:
  //   Sample Circuit
endmodule

module NAND2 (
  input  A,
  input  B,
  output RESULT
);

  wire and_1_out;

  and and_1 (and_1_out, A, B);
  not not_1 (RESULT, and_1_out);
endmodule

module NOR2 (
  input  A,
  input  B,
  output RESULT
);

  wire or_1_out;

  or or_1 (or_1_out, A, B);
  not not_1 (RESULT, or_1_out);
endmodule

module XOR2 (
  input  A,
  input  B,
  output RESULT
);

  wire and_1_out, and_2_out, not_1_out, not_2_out, or_1_out;

  not not_1 (not_1_out, B);
  not not_2 (not_2_out, A);
  and and_1 (and_1_out, A, B);
  and and_2 (and_2_out, not_1_out, not_2_out);
  or or_1 (or_1_out, and_1_out, and_2_out);
  not not_3 (RESULT, or_1_out);
endmodule

module MUX2 (
  input  A,
  input  B,
  input  SEL,
  output RESULT
);

  wire and_1_out, and_2_out, not_1_out;

  not not_1 (not_1_out, SEL);
  and and_1 (and_1_out, A, not_1_out);
  and and_2 (and_2_out, B, SEL);
  or or_1 (RESULT, and_1_out, and_2_out);
endmodule

module MUX4 (
  input  A,
  input  B,
  input  C,
  input  D,
  input  SEL0,
  input  SEL1,
  output RESULT
);

  wire and_1_out, and_2_out, and_3_out, and_4_out, and_5_out, not_1_out, not_2_out, not_3_out, not_4_out,
       not_5_out, or_1_out, or_2_out, or_3_out, or_4_out, or_5_out;

  not not_1 (not_1_out, SEL0);
  not not_2 (not_2_out, SEL1);
  or or_1 (or_1_out, SEL0, SEL1);
  or or_2 (or_2_out, not_1_out, SEL1);
  or or_3 (or_3_out, SEL0, not_2_out);
  and and_1 (and_1_out, SEL0, SEL1);
  not not_3 (not_3_out, or_1_out);
  not not_4 (not_4_out, or_2_out);
  not not_5 (not_5_out, or_3_out);
  and and_2 (and_2_out, A, not_3_out);
  and and_3 (and_3_out, B, not_4_out);
  and and_4 (and_4_out, C, not_5_out);
  and and_5 (and_5_out, D, and_1_out);
  or or_4 (or_4_out, and_2_out, and_3_out);
  or or_5 (or_5_out, and_4_out, and_5_out);
  or or_6 (RESULT, or_4_out, or_5_out);
endmodule
